// Logisim project adder_circuit.circ as structural Verilog: 1 circuit, main circuit main
module main (
  input  Cin,
  input  B0,
  input  B1,
  input  B2,
  input  B3,
  input  A0,
  input  A1,
  input  A2,
  input  A3
);

  wire and_1_out, and_2_out, and_3_out, and_4_out, and_5_out, and_6_out, and_7_out, and_8_out, or_1_out,
       or_2_out, or_3_out, or_4_out, xor_1_out, xor_2_out, xor_3_out, xor_4_out, xor_5_out, xor_6_out,
       xor_7_out, xor_8_out;

  xor xor_1 (xor_1_out, A0, B0);
  xor xor_2 (xor_2_out, A1, B1);
  buf and_1 (and_1_out, A1);  // AND_Gate
  xor xor_3 (xor_3_out, A2, B2);
  and and_2 (and_2_out, B2, A2);
  xor xor_4 (xor_4_out, A3, B3);
  and and_3 (and_3_out, A3, B3);
  and and_4 (and_4_out, xor_1_out, Cin);
  and and_5 (and_5_out, A0, B0);
  xor xor_5 (xor_5_out, xor_1_out, Cin);
  and and_6 (and_6_out, xor_2_out, or_3_out);
  and and_7 (and_7_out, or_1_out, xor_3_out);
  and and_8 (and_8_out, xor_4_out, or_2_out);
  xor xor_6 (xor_6_out, or_3_out, xor_2_out);
  or or_1 (or_1_out, and_1_out, and_6_out);
  xor xor_7 (xor_7_out, or_1_out, xor_3_out);
  or or_2 (or_2_out, and_7_out, and_2_out);
  xor xor_8 (xor_8_out, xor_4_out, or_2_out);
  or or_3 (or_3_out, and_4_out, and_5_out);
  or or_4 (or_4_out, and_3_out, and_8_out);
  LED S0_LSB (.in(xor_5_out));
  LED S1 (.in(xor_6_out));
  LED S2 (.in(xor_7_out));
  LED S3_MSB (.in(xor_8_out));
  LED Cout (.in(or_4_out));

  // Notes on the sheet:
  //   C0
  //   C1
  //   C2
  //   C0
endmodule
